# Fritzing sketch Circuit (saved by Fritzing 0.9.3b)
circuit board: 8.46667cm x 5.64444cm
breadboards: 1

parts:
  Composant1 = Arduino Uno (Rev3)
  Q1 = NPN-Transistor [part_number=2N3904 package="TO92 [THT]"]
  R1 = Resistor [tolerance=±5% resistance=4.7k package="0805 [SMD]"]
  U2 = MOC3031-M [package=dil06]
  R2 = Resistor [tolerance=±5% resistance=100 package="0805 [SMD]"]

nets:
  N1: Composant1.A1, R1.Pin_0
  N2: Composant1.5V, R2.Pin_0
  N3: Composant1.GND, U2.2
  N4: Q1.E, U2.1
  N5: Q1.B, R1.Pin_1
  N6: Q1.C, R2.Pin_1
